# Fritzing sketch TheGreatRandomCube (saved by Fritzing 0.9.6b)
breadboards: 1

parts:
  Part1 = Arduino Nano (Rev3.0)
  LED1 = LED - 5mm [color="White (6500K)" current=0.030 package="5 mm [THT]"]
  LED2 = LED - 5mm [color="White (6500K)" current=0.030 package="5 mm [THT]"]
  LED3 = LED - 5mm [color="White (6500K)" current=0.030 package="5 mm [THT]"]
  LED4 = LED - 5mm [color="White (6500K)" current=0.030 package="5 mm [THT]"]
  LED5 = LED - 5mm [color="White (6500K)" current=0.030 package="5 mm [THT]"]
  LED6 = LED - 5mm [color="White (6500K)" current=0.030 package="5 mm [THT]"]
  R1 = Resistor [tolerance=±5% power=0.25 resistance=560 package=THT]
  R2 = Resistor [tolerance=±5% power=0.25 resistance=560 package=THT]
  R3 = Resistor [tolerance=±5% power=0.25 resistance=560 package=THT]
  R4 = Resistor [tolerance=±5% power=0.25 resistance=560 package=THT]
  R5 = Resistor [tolerance=±5% power=0.25 resistance=560 package=THT]
  R6 = Resistor [tolerance=±5% power=0.25 resistance=560 package=THT]

nets:
  N1: Part1.GND, LED1.cathode, LED2.cathode, LED3.cathode, LED4.cathode, LED5.cathode, LED6.cathode
  N2: Part1.D2, Part1.D4, Part1.D6
  N3: Part1.D3, Part1.D5, Part1.D7
  N4: LED1.anode, R4.Pin_1, R5.Pin_1, R6.Pin_1
  N5: LED2.anode, LED3.anode
  N6: LED4.anode, R1.Pin_1, R2.Pin_1, R3.Pin_1
  N7: LED5.anode, LED6.anode
  N8: R1.Pin_0, R2.Pin_0, R3.Pin_0
  N9: R4.Pin_0, R5.Pin_0, R6.Pin_0

notes:
  The Great Random Cube
  Author: SadBarin
  Date: 17.06.2021
  For Arduino Nano Atmega 328
